// Logisim project 2-1(芯片).circ as structural Verilog: 1 circuit, main circuit main
module main (
  input  A,
  input  B,
  input  Cin,
  output S,
  output Cout
);

  wire n7400_1_p4, n7400_1_p7, n7400_1_p12, n7486_1_p3;

  // _7486 7486_1: pin names not known; wires that end beside it: A, B, n7486_1_p3, n7486_1_p3, Cin, S, 1'b1
  // _7400 7400_1: pin names not known; wires that end beside it: 1'b0, A, B, n7400_1_p4, Cin, A, n7400_1_p7, 1'b0, 1'b1, B, Cin, n7400_1_p12
  // _7410 7410_1: pin names not known; wires that end beside it: n7400_1_p7, n7400_1_p4, 1'b0, 1'b1, n7400_1_p12, Cout
endmodule
