// Logisim project 2-2-1.circ as structural Verilog: 1 circuit, main circuit main
module main (
  input  Cin,
  input  A,
  input  B,
  output S,
  output Cout
);

  wire n7404_1_p2, n7420_1_p1, n7420_1_p6, n7420_1_p9, n74139_1_p4, n74139_1_p5, n74139_1_p10, n74139_1_p11;

  // _7404 7404_1: pin names not known; wires that end beside it: Cin, n7404_1_p2, 1'b0, 1'b1, 1'b1
  // _74139 74139_1: pin names not known; wires that end beside it: Cin, A, B, n74139_1_p4, n74139_1_p5, 1'b1, n7404_1_p2, A, B, n74139_1_p10, n74139_1_p11
  // _7420 7420_1: pin names not known; wires that end beside it: n7420_1_p1, 1'b0, n74139_1_p5, n74139_1_p4, n74139_1_p10, n7420_1_p6, S, 1'b0, n7420_1_p9, n7420_1_p6, 1'b1, n7420_1_p1, n7420_1_p6, n7420_1_p9, n74139_1_p11, Cout
endmodule
