// Logisim project 2-2-2.circ as structural Verilog: 1 circuit, main circuit main
module main (
  input  Cin,
  input  A,
  input  B,
  output Cout,
  output S
);

  wire n7404_1_p2;

  // _7404 7404_1: pin names not known; wires that end beside it: Cin, n7404_1_p2, 1'b0, 1'b1
  // _74153 74153_1: pin names not known; wires that end beside it: 1'b0, B, Cin, n7404_1_p2, n7404_1_p2, Cin, S, 1'b0, 1'b1, 1'b0, A, 1'b1, Cin, Cin, 1'b0, Cout, Cout
endmodule
