// Logisim project 2-3(芯片).circ as structural Verilog: 1 circuit, main circuit main
module main (
  input  X3,
  input  X2,
  input  X1,
  input  X0,
  output F
);

  wire n7404_1_p1, n7404_1_p4, n7486_1_p3;

  // _7486 7486_1: pin names not known; wires that end beside it: X3, X2, n7486_1_p3, n7486_1_p3, X1, 1'b1
  // _7404 7404_1: pin names not known; wires that end beside it: n7404_1_p1, 1'b0, n7404_1_p1, n7404_1_p4, 1'b1
  // _7400 7400_1: pin names not known; wires that end beside it: 1'b0, n7404_1_p4, X0, F, 1'b0, 1'b1
endmodule
