// Logisim project 2-3(逻辑门).circ as structural Verilog: 1 circuit, main circuit main
module main (
  input  X3,
  input  X2,
  input  X1,
  input  X0,
  output F
);

  wire not_1_out, xor_1_out, xor_2_out;

  xor xor_1 (xor_1_out, X3, X2);
  xor xor_2 (xor_2_out, xor_1_out, X1);
  not not_1 (not_1_out, xor_2_out);
  nand nand_1 (F, not_1_out, X0);
endmodule
