// Logisim project 2-4.circ as structural Verilog: 2 circuits, main circuit main
module main (
  input  DU1,
  input  DU2,
  input  DU3,
  input  DU4,
  input  DU5,
  input  DU6,
  input  DU7,
  output NOERROR_L,
  output DC_L1,
  output DC_L2,
  output DC_L3,
  output DC_L4,
  output DC_L5,
  output DC_L6,
  output DC_L7
);

  wire n74x280_1_even, n74x280_1_odd, n74x280_2_even, n74x280_2_odd, n74x280_3_even, n74x280_3_odd,
       n74138_1_p10, n74138_1_p12, n74138_1_p13, n74138_1_p14, n74138_1_p15, n74138_1_p16, n74138_1_p17;

  _74x280 u_74x280_1 (
    .A(DU7), .B(DU5), .C(DU3), .D(DU1), .E(1'b0), .F(1'b0), .G(1'b0), .H(1'b0), .I(1'b0),
    .EVEN(n74x280_1_even), .ODD(n74x280_1_odd));
  _74x280 u_74x280_2 (
    .A(DU7), .B(DU6), .C(DU3), .D(DU2), .E(1'b0), .F(1'b0), .G(1'b0), .H(1'b0), .I(1'b0),
    .EVEN(n74x280_2_even), .ODD(n74x280_2_odd));
  _74x280 u_74x280_3 (
    .A(DU7), .B(DU6), .C(DU5), .D(DU4), .E(1'b0), .F(1'b0), .G(1'b0), .H(1'b0), .I(1'b0),
    .EVEN(n74x280_3_even), .ODD(n74x280_3_odd));
  // _74138 74138_1: pin names not known; wires that end beside it: n74x280_1_even, n74x280_2_even, n74x280_3_even, n74x280_1_odd, n74x280_2_odd, n74x280_3_odd, 1'b0, 1'b0, 1'b1, n74138_1_p10, NOERROR_L, n74138_1_p12, n74138_1_p13, n74138_1_p14, n74138_1_p15, n74138_1_p16, n74138_1_p17
  xnor xnor_1 (DC_L1, DU1, ~n74138_1_p12);  // XNOR_Gate
  xnor xnor_2 (DC_L2, DU2, ~n74138_1_p13);  // XNOR_Gate
  xnor xnor_3 (DC_L3, DU3, ~n74138_1_p14);  // XNOR_Gate
  xnor xnor_4 (DC_L4, DU4, ~n74138_1_p15);  // XNOR_Gate
  xnor xnor_5 (DC_L5, DU5, ~n74138_1_p16);  // XNOR_Gate
  xnor xnor_6 (DC_L6, DU6, ~n74138_1_p17);  // XNOR_Gate
  xnor xnor_7 (DC_L7, DU7, ~n74138_1_p10);  // XNOR_Gate
endmodule

module _74x280 (
  input  A,
  input  B,
  input  C,
  input  D,
  input  E,
  input  F,
  input  G,
  input  H,
  input  I,
  output EVEN,
  output ODD
);

  wire not_1_out, xor_1_out, xor_2_out, xor_3_out, xor_4_out, xor_5_out, xor_6_out, xor_7_out, xor_8_out;

  xor xor_1 (xor_1_out, A, B);
  xor xor_2 (xor_2_out, D, E);
  xor xor_3 (xor_3_out, G, H);
  xor xor_4 (xor_4_out, xor_1_out, C);
  xor xor_5 (xor_5_out, xor_2_out, F);
  xor xor_6 (xor_6_out, xor_3_out, I);
  not not_1 (not_1_out, xor_6_out);
  xor xor_7 (xor_7_out, xor_4_out, xor_5_out);
  xor xor_8 (xor_8_out, xor_4_out, xor_5_out);
  xor xor_9 (EVEN, xor_7_out, not_1_out);
  xor xor_10 (ODD, xor_8_out, xor_6_out);
endmodule
