// Logisim project 4-1-1.circ as structural Verilog: 1 circuit, main circuit main
module main (
  input  LOAD_L,
  output out_2,
  output out_3,
  output out_4,
  output out_5
);

  wire CLOCK_out, n74161_1_p1;

  Clock CLOCK (.out(CLOCK_out));
  // _74161 74161_1: pin names not known; wires that end beside it: n74161_1_p1, CLOCK_out, 1'b0, 1'b0, 1'b0, 1'b0, 1'b1, 1'b0, 1'b1, out_2, out_3, out_4, out_5, 1'b1, LOAD_L
  nand nand_1 (n74161_1_p1, out_5, out_4);
endmodule
