// Logisim project 4-1-2.circ as structural Verilog: 1 circuit, main circuit main
module main (
  input  CLR_L,
  output out_2,
  output out_3,
  output out_4,
  output out_5
);

  wire CLOCK_out, n74163_1_p15;

  Clock CLOCK (.out(CLOCK_out));
  // _74163 74163_1: pin names not known; wires that end beside it: CLR_L, CLOCK_out, 1'b1, 1'b1, 1'b0, 1'b0, 1'b1, 1'b0, 1'b1, out_2, out_3, out_4, out_5, 1'b1, n74163_1_p15
  nand nand_1 (n74163_1_p15, out_5, out_4, out_3);
endmodule
