// Logisim project 4-2.circ as structural Verilog: 1 circuit, main circuit main
module main (
  output X0,
  output X4,
  output X8,
  output X1,
  output X5,
  output X9,
  output X2,
  output X6,
  output X10,
  output X3,
  output X7,
  output X11
);

  wire CLOCK_out, n74163_1_p1, n74163_1_p15, n74163_2_p1, not_1_out, not_2_out;

  Clock CLOCK (.out(CLOCK_out));
  // _74163 74163_1: pin names not known; wires that end beside it: n74163_1_p1, CLOCK_out, 1'b1, 1'b0, 1'b0, 1'b0, 1'b1, 1'b0, 1'b1, X0, X1, X2, X3, 1'b1, n74163_1_p15
  nand nand_1 (n74163_1_p1, X0, X3);
  not not_1 (not_1_out, n74163_1_p1);
  // _74163 74163_2: pin names not known; wires that end beside it: n74163_2_p1, CLOCK_out, 1'b0, 1'b0, 1'b0, 1'b0, not_1_out, 1'b0, 1'b1, X4, X5, X6, X7, 1'b1, n74163_1_p15
  nand nand_2 (n74163_2_p1, X4, X7, not_1_out, 1'b1);
  not not_2 (not_2_out, n74163_2_p1);
  // _74163 74163_3: pin names not known; wires that end beside it: 1'b1, CLOCK_out, 1'b0, 1'b0, 1'b0, 1'b0, not_2_out, 1'b0, 1'b1, X8, X9, X10, X11, 1'b1, n74163_1_p15
  nand nand_3 (n74163_1_p15, X8, X4, X6, X2);
endmodule
