// Logisim project 4-3.circ as structural Verilog: 2 circuits, main circuit main
module main (
  input  CLR_L,
  output out_2,
  output out_3,
  output out_4,
  output out_5
);

  wire CLOCK_out, n7402_1_p1, n7402_1_p2, n7402_1_p9, n7486_1_p3, n7486_1_p6;

  Clock CLOCK (.out(CLOCK_out));
  _74x194 u_74x194_1 (
    .S1(1'b1), .S0(1'b0), .CLOCK(CLOCK_out), .CLEAR(CLR_L), .SHIFT_LEFT_SERIAL_INPUT(n7486_1_p6), .A(1'b0),
    .B(1'b0), .C(1'b0), .D(1'b0), .QA(out_2), .QB(out_3), .QC(out_4), .QD(out_5));  // open: SHIFT_RIGHT_SERIAL_INPUT
  // _7402 7402_1: pin names not known; wires that end beside it: n7402_1_p1, n7402_1_p2, n7402_1_p2, n7402_1_p2, out_3, out_4, 1'b0, 1'b1, n7402_1_p9, out_5, n7402_1_p1
  // _7486 7486_1: pin names not known; wires that end beside it: out_2, out_3, n7486_1_p3, n7486_1_p3, n7402_1_p9, n7486_1_p6, 1'b0, 1'b1
endmodule

// 74194
module _74x194 (
  input  A,
  input  B,
  input  C,
  input  D,
  input  S1,
  input  S0,
  input  SHIFT_LEFT_SERIAL_INPUT,
  input  SHIFT_RIGHT_SERIAL_INPUT,
  input  CLOCK,
  input  CLEAR,
  output QA,
  output QB,
  output QC,
  output QD
);

  wire and_1_out, and_2_out, and_3_out, and_4_out, and_5_out, and_6_out, and_7_out, and_8_out, and_9_out,
       and_10_out, and_11_out, and_12_out, and_13_out, and_14_out, and_15_out, and_16_out, nor_1_out,
       nor_2_out, nor_3_out, nor_4_out, not_1_out, not_2_out, not_3_out, not_4_out, not_5_out, not_6_out,
       not_7_out;

  not not_1 (not_1_out, S1);
  not not_2 (not_2_out, S0);
  and and_1 (and_1_out, SHIFT_RIGHT_SERIAL_INPUT, not_1_out, S0);
  not not_3 (not_3_out, CLEAR);
  and and_2 (and_2_out, S0, S1, A);
  and and_3 (and_3_out, not_2_out, S1, QB);
  nor nor_1 (nor_1_out, and_1_out, and_2_out, and_3_out, and_4_out);
  not not_4 (not_4_out, nor_1_out);
  and and_4 (and_4_out, S0, not_1_out, QA);
  S_R_Flip_Flop s_r_ff_1 (
    .S(not_4_out), .clk(CLOCK), .R(nor_1_out), .Q(QA), .reset(not_3_out));  // open: Qn, preset, en
  and and_5 (and_5_out, QA, not_1_out, S0);
  and and_6 (and_6_out, S0, S1, B);
  nor nor_2 (nor_2_out, and_5_out, and_6_out, and_7_out, and_8_out);
  and and_7 (and_7_out, not_2_out, S1, QC);
  and and_8 (and_8_out, not_2_out, not_1_out, QB);
  not not_5 (not_5_out, nor_2_out);
  S_R_Flip_Flop s_r_ff_2 (
    .S(not_5_out), .clk(CLOCK), .R(nor_2_out), .Q(QB), .reset(not_3_out));  // open: Qn, preset, en
  and and_9 (and_9_out, QB, not_1_out, S0);
  and and_10 (and_10_out, S0, S1, C);
  and and_11 (and_11_out, not_2_out, S1, QD);
  nor nor_3 (nor_3_out, and_9_out, and_10_out, and_11_out, and_12_out);
  not not_6 (not_6_out, nor_3_out);
  and and_12 (and_12_out, not_1_out, not_2_out, QC);
  S_R_Flip_Flop s_r_ff_3 (
    .S(not_6_out), .clk(CLOCK), .R(nor_3_out), .Q(QC), .reset(not_3_out));  // open: Qn, preset, en
  and and_13 (and_13_out, QC, not_1_out, S0);
  and and_14 (and_14_out, S0, S1, D);
  nor nor_4 (nor_4_out, and_13_out, and_14_out, and_15_out, and_16_out);
  and and_15 (and_15_out, not_2_out, S1, SHIFT_LEFT_SERIAL_INPUT);
  and and_16 (and_16_out, not_2_out, not_1_out, QD);
  not not_7 (not_7_out, nor_4_out);
  S_R_Flip_Flop s_r_ff_4 (
    .S(not_7_out), .clk(CLOCK), .R(nor_4_out), .Q(QD), .reset(not_3_out));  // open: Qn, preset, en
endmodule
