// Logisim project 4-4.circ as structural Verilog: 1 circuit, main circuit main
module main (
  input  CLR_L,
  output out_2,
  output out_3,
  output out_4,
  output out_5
);

  wire CLOCK_out, dip_7400_1_p3, dip_7400_1_p6, dip_7400_1_p9, dip_7404_1_p2, dip_7404_1_p4, dip_7404_1_p6,
       dip_7404_1_p8, dip_7420_1_p4, dip_7420_1_p5;

  Clock CLOCK (.out(CLOCK_out));
  _74x194 u_74x194_1 (
    .S1(1'b1), .S0(1'b0), .CLOCK(CLOCK_out), .CLEAR(CLR_L), .SHIFT_LEFT_SERIAL_INPUT(dip_7420_1_p5),
    .A(1'b0), .B(1'b0), .C(1'b0), .D(1'b0), .QA(out_2), .QB(out_3), .QC(out_4), .QD(out_5));  // open: SHIFT_RIGHT_SERIAL_INPUT
  // DIP_7404 dip_7404_1: pin names not known; wires that end beside it: out_2, dip_7404_1_p2, out_3, dip_7404_1_p4, out_4, dip_7404_1_p6, out_5, dip_7404_1_p8
  // DIP_7400 dip_7400_1: pin names not known; wires that end beside it: dip_7404_1_p2, out_5, dip_7400_1_p3, dip_7404_1_p4, dip_7404_1_p6, dip_7400_1_p6, out_5, dip_7404_1_p6, dip_7400_1_p9
  // DIP_7420 dip_7420_1: pin names not known; wires that end beside it: dip_7400_1_p9, dip_7400_1_p6, dip_7400_1_p3, dip_7420_1_p4, dip_7420_1_p5, out_2, out_4, 1'b1, dip_7404_1_p8, dip_7420_1_p4
endmodule
