// Logisim project 4-6.circ as structural Verilog: 1 circuit, main circuit main
module main (
  output out_1,
  output out_2,
  output out_3,
  output out_4
);

  wire clock_1_out, d_ff_3_qn, nand_1_out, nand_2_out;

  Clock clock_1 (.out(clock_1_out));
  nand nand_1 (nand_1_out, out_1, nand_2_out);
  D_Flip_Flop d_ff_1 (
    .clk(clock_1_out), .D(nand_1_out), .Q(out_4), .preset(1'b0), .en(1'b1), .reset(1'b0));  // open: Qn
  nand nand_2 (nand_2_out, d_ff_3_qn, out_3);
  D_Flip_Flop d_ff_2 (.clk(clock_1_out), .D(out_4), .Q(out_3), .preset(1'b0), .en(1'b1), .reset(1'b0));  // open: Qn
  D_Flip_Flop d_ff_3 (.clk(clock_1_out), .D(out_3), .Q(out_2), .Qn(d_ff_3_qn), .preset(1'b0), .en(1'b1), .reset(1'b0));
  D_Flip_Flop d_ff_4 (.clk(clock_1_out), .D(out_2), .Q(out_1), .preset(1'b0), .en(1'b1), .reset(1'b0));  // open: Qn
endmodule
