// Logisim project 4-7-1.circ as structural Verilog: 1 circuit, main circuit main
module main (
  input  CLR_L,
  input  INPUT,
  output A7,
  output A6,
  output A5,
  output A4,
  output A3,
  output A2,
  output A1,
  output A0,
  output FINISH
);

  wire CLOCK_out, n74x194_3_qd, nand_1_out, not_1_out;

  Clock CLOCK (.out(CLOCK_out));
  _74x194 u_74x194_1 (
    .S1(1'b1), .S0(FINISH), .CLOCK(CLOCK_out), .CLEAR(CLR_L), .SHIFT_LEFT_SERIAL_INPUT(INPUT), .A(1'b1),
    .B(1'b1), .C(1'b0), .D(INPUT), .QA(A3), .QB(A2), .QC(A1), .QD(A0));  // open: SHIFT_RIGHT_SERIAL_INPUT
  _74x194 u_74x194_2 (
    .S1(1'b1), .S0(FINISH), .CLOCK(CLOCK_out), .CLEAR(CLR_L), .SHIFT_LEFT_SERIAL_INPUT(A3), .A(1'b1),
    .B(1'b1), .C(1'b1), .D(1'b1), .QA(A7), .QB(A6), .QC(A5), .QD(A4));  // open: SHIFT_RIGHT_SERIAL_INPUT
  _74x194 u_74x194_3 (
    .S1(1'b1), .S0(not_1_out), .CLOCK(CLOCK_out), .CLEAR(1'b1), .SHIFT_LEFT_SERIAL_INPUT(A7), .A(1'b1),
    .B(1'b1), .C(1'b1), .D(1'b1), .QD(n74x194_3_qd));  // open: SHIFT_RIGHT_SERIAL_INPUT, QA, QB, QC
  not not_1 (not_1_out, nand_1_out);
  not not_2 (FINISH, n74x194_3_qd);
  nand nand_1 (nand_1_out, FINISH, CLR_L);
endmodule
