// Logisim project 4-7-2.circ as structural Verilog: 1 circuit, main circuit main
module main (
  input  CLR_L,
  input  X7,
  input  X6,
  input  X5,
  input  X4,
  input  X3,
  input  X2,
  input  X1,
  input  X0,
  input  IN_SIG,
  output OUTPUT,
  output OUT_SIG
);

  wire CLOCK_out, n74x194_2_qa;

  Clock CLOCK (.out(CLOCK_out));
  _74x194 u_74x194_1 (
    .S1(1'b1), .S0(IN_SIG), .CLOCK(CLOCK_out), .CLEAR(CLR_L), .SHIFT_LEFT_SERIAL_INPUT(n74x194_2_qa), .A(X7),
    .B(X6), .C(X5), .D(X4), .QA(OUTPUT));  // open: SHIFT_RIGHT_SERIAL_INPUT, QB, QC, QD
  _74x194 u_74x194_2 (
    .S1(1'b1), .S0(IN_SIG), .CLOCK(CLOCK_out), .CLEAR(CLR_L), .SHIFT_LEFT_SERIAL_INPUT(1'b0), .A(X3), .B(X2),
    .C(X1), .D(X0), .QA(n74x194_2_qa));  // open: SHIFT_RIGHT_SERIAL_INPUT, QB, QC, QD
  not not_1 (OUT_SIG, IN_SIG);
endmodule
